# Fritzing sketch lcd (saved by Fritzing 0.9.3b)
breadboards: 1

parts:
  C1 = Electrolytic Capacitor [capacitance=1µF package="100 mil [THT, electrolytic]"]
  R2 = Resistor [tolerance=±5% resistance=220 package=THT]
  LCD1 = LCD screen
  10k = Rotary Potentiometer (Small) [maximum_resistance=100kΩ package=THT]
  JP2 = Header 6 [package=1x06_smd_straight_alt]

nets:
  GND: C1.-, LCD1.VSS, LCD1.R/W, LCD1.LED-, 10k.leg1
  5V: C1.+, LCD1.VDD
  N1: R2.Pin_0, 10k.leg2
  N2: R2.Pin_1, LCD1.LED+
  N3: LCD1.V0, 10k.wiper
  N4: LCD1.RS, JP2.6
  N5: LCD1.E, JP2.5
  N6: LCD1.DB4, JP2.4
  N7: LCD1.DB5, JP2.3
  N8: LCD1.DB6, JP2.2
  N9: LCD1.DB7, JP2.1
